# Fritzing sketch ironMan-Helmet (saved by Fritzing 0.9.4)

parts:
  ULN2003 = ULN2003A [package="DIP16 [THT]"]
  SPKR1 = Loudspeaker
  DFRobot_DFPlayer_Mini1 = DFRobot DFPlayer Mini [part_number=DFR0299]
  U1 = LIPO-2000mAh [package=lipo-2000]
  Bauteil1 = Power Cell LiPo Charger/Booster
  J2 = Basic Servo
  M5Stack1 = M5Atom
  J1 = Basic Servo

nets:
  N1: ULN2003.In_1, M5Stack1.G21
  N2: ULN2003.In_2, M5Stack1.G25
  GND: ULN2003.0V, DFRobot_DFPlayer_Mini1.GND-1, DFRobot_DFPlayer_Mini1.GND-2, U1.-, Bauteil1.GND, M5Stack1.Gnd
  VCC: ULN2003.COM_-_Common, DFRobot_DFPlayer_Mini1.VCC, Bauteil1.VCC, J2.vcc, M5Stack1.5v, J1.vcc
  N3: ULN2003.Out_2, J2.gnd
  N4: ULN2003.Out_1, J1.gnd
  N5: SPKR1.pin1, DFRobot_DFPlayer_Mini1.SPK_2
  N6: SPKR1.pin2, DFRobot_DFPlayer_Mini1.SPK_1
  N7: DFRobot_DFPlayer_Mini1.RX, M5Stack1.G23
  N8: DFRobot_DFPlayer_Mini1.TX, M5Stack1.G33
  N9: U1.+, Bauteil1.VBATT
  N10: J2.pulse, M5Stack1.G19
  N11: M5Stack1.G22, J1.pulse

custom parts:
  M5Atom: M5Atom is a mini M5Stack, powered by ESP32 pico chip. It is a portable, easy-to-use, open source, IoT development board.
